// Logisim project Contador em Anel.circ as structural Verilog: 2 circuits, main circuit main
module main (
  input  Clock,
  input  Enable,
  input  INICIO,
  input  Clock_2,
  input  Enable_2,
  input  INICIO_2,
  output Q0,
  output Q1,
  output Q2,
  output Q3,
  output Q0_2,
  output Q1_2,
  output Q2_2,
  output Q3_2
);

  wire d_ff_8_qn;

  FF_JK_Controlado ff_jk_controlado_1 ();  // open: J, CLK, K, sPRE, sCLR, enCLK, Q, nQ, CLR
  D_Flip_Flop d_ff_1 (.clk(Clock), .D(Q3), .Q(Q0), .preset(INICIO), .en(Enable), .reset(1'b0));  // open: Qn
  D_Flip_Flop d_ff_2 (
    .clk(Clock_2), .D(d_ff_8_qn), .Q(Q0_2), .preset(1'b0), .en(Enable_2), .reset(INICIO_2));  // open: Qn
  D_Flip_Flop d_ff_3 (.clk(Clock), .D(Q0), .Q(Q1), .preset(1'b0), .en(Enable), .reset(INICIO));  // open: Qn
  D_Flip_Flop d_ff_4 (.clk(Clock_2), .D(Q0_2), .Q(Q1_2), .preset(1'b0), .en(Enable_2), .reset(INICIO_2));  // open: Qn
  D_Flip_Flop d_ff_5 (.clk(Clock), .D(Q1), .Q(Q2), .preset(1'b0), .en(Enable), .reset(INICIO));  // open: Qn
  D_Flip_Flop d_ff_6 (.clk(Clock_2), .D(Q1_2), .Q(Q2_2), .preset(1'b0), .en(Enable_2), .reset(INICIO_2));  // open: Qn
  D_Flip_Flop d_ff_7 (.clk(Clock), .D(Q2), .Q(Q3), .preset(1'b0), .en(Enable), .reset(INICIO));  // open: Qn
  D_Flip_Flop d_ff_8 (
    .clk(Clock_2), .D(Q2_2), .Q(Q3_2), .Qn(d_ff_8_qn), .preset(1'b0), .en(Enable_2), .reset(INICIO_2));
  Hex_Digit_Display hex_digit_display_1 (.value({Q3, Q2, Q1, Q0}));  // open: dp
  Hex_Digit_Display hex_digit_display_2 (.value({Q3_2, Q2_2, Q1_2, Q0_2}));  // open: dp

  // Notes on the sheet:
  //   Contador em Anel
  //   Contador em Anel Torcido
endmodule

module FF_JK_Controlado (
  input  J,
  input  CLK,
  input  K,
  input  sPRE,
  input  sCLR,
  input  enCLK,
  input  CLR,
  output Q,
  output nQ
);

  wire and_1_out, and_2_out, and_3_out, and_4_out, not_1_out, not_2_out, or_1_out, or_2_out;

  or or_1 (or_1_out, J, sPRE);
  and and_1 (and_1_out, K, not_1_out);
  not not_1 (not_1_out, sPRE);
  and and_2 (and_2_out, or_1_out, not_2_out);
  not not_2 (not_2_out, sCLR);
  or or_2 (or_2_out, and_1_out, sCLR);
  and and_3 (and_3_out, and_2_out, enCLK);
  and and_4 (and_4_out, or_2_out, enCLK);
  J_K_Flip_Flop j_k_ff_1 (
    .J(and_3_out), .clk(CLK), .K(and_4_out), .Q(Q), .Qn(nQ), .preset(1'b0), .en(1'b1), .reset(CLR));
endmodule
