// Logisim project Exercicio1.circ as structural Verilog: 1 circuit, main circuit main
module main (
);

  wire _0001_out, and_1_out, and_2_out, clock_1_out, j_k_ff_1_q, j_k_ff_2_q, j_k_ff_3_q, j_k_ff_4_q, Q0, Q1,
       Q2, Q3, t_ff_1_q, VOLTA_PRA_0001;

  Clock clock_1 (.out(clock_1_out));
  Hex_Digit_Display hex_digit_display_1 (.value({Q3, Q2, Q1, Q0}));  // open: dp
  T_Flip_Flop t_ff_1 (.clk(_0001_out), .T(1'b1), .Q(t_ff_1_q), .en(1'b1));  // open: Qn, preset, reset
  xor xor_1 (Q0, t_ff_1_q, j_k_ff_1_q);
  J_K_Flip_Flop j_k_ff_1 (
    .J(1'b1), .clk(clock_1_out), .K(1'b1), .Q(j_k_ff_1_q), .preset(VOLTA_PRA_0001), .en(1'b1));  // open: Qn, reset
  xor xor_2 (Q1, t_ff_1_q, j_k_ff_2_q);
  J_K_Flip_Flop j_k_ff_2 (
    .J(j_k_ff_1_q), .clk(clock_1_out), .K(j_k_ff_1_q), .Q(j_k_ff_2_q), .en(1'b1), .reset(VOLTA_PRA_0001));  // open: Qn, preset
  and _0000 (VOLTA_PRA_0001, ~j_k_ff_1_q, ~j_k_ff_2_q, ~j_k_ff_3_q, ~j_k_ff_4_q);  // AND_Gate
  and _0001 (_0001_out, j_k_ff_1_q, ~j_k_ff_2_q, ~j_k_ff_3_q, ~j_k_ff_4_q);  // AND_Gate
  and and_1 (and_1_out, j_k_ff_1_q, j_k_ff_2_q);
  xor xor_3 (Q2, t_ff_1_q, j_k_ff_3_q);
  J_K_Flip_Flop j_k_ff_3 (
    .J(and_1_out), .clk(clock_1_out), .K(and_1_out), .Q(j_k_ff_3_q), .en(1'b1), .reset(VOLTA_PRA_0001));  // open: Qn, preset
  and and_2 (and_2_out, and_1_out, j_k_ff_3_q);
  xor xor_4 (Q3, t_ff_1_q, j_k_ff_4_q);
  J_K_Flip_Flop j_k_ff_4 (
    .J(and_2_out), .clk(clock_1_out), .K(and_2_out), .Q(j_k_ff_4_q), .en(1'b1), .reset(VOLTA_PRA_0001));  // open: Qn, preset
endmodule
