// Logisim project Exercicio2.circ as structural Verilog: 1 circuit, main circuit main
module main (
  output out_1
);

  wire and_1_out, clock_1_out, subclock, t_ff_1_q, t_ff_2_q, t_ff_3_q;

  Clock clock_1 (.out(clock_1_out));
  T_Flip_Flop t_ff_1 (
    .clk(clock_1_out), .T(clock_1_out), .Q(t_ff_1_q), .reset(subclock), .en(1'b1));  // open: Qn, preset
  T_Flip_Flop t_ff_2 (.clk(clock_1_out), .T(t_ff_1_q), .Q(t_ff_2_q), .reset(subclock), .en(1'b1));  // open: Qn, preset
  and and_1 (and_1_out, t_ff_1_q, t_ff_2_q);
  and and_2 (subclock, t_ff_1_q, t_ff_3_q);
  T_Flip_Flop t_ff_3 (.clk(clock_1_out), .T(and_1_out), .Q(t_ff_3_q), .reset(subclock), .en(1'b1));  // open: Qn, preset
  T_Flip_Flop t_ff_4 (.clk(subclock), .T(subclock), .Q(out_1), .en(1'b1));  // open: Qn, preset, reset
endmodule
