// Logisim project Exercicio3.circ as structural Verilog: 1 circuit, main circuit main
module main (
  output out_1
);

  wire and_1_out, and_2_out, and_3_out, and_4_out, and_5_out, and_6_out, and_7_out, and_9_out, and_10_out,
       and_11_out, and_12_out, and_13_out, and_14_out, and_15_out, and_16_out, and_17_out, and_18_out,
       and_19_out, and_20_out, and_21_out, and_22_out, bit1, bit4, bit5, bit9, bit12, bit14, bit15, bit17,
       clock_1_out, subclock, t_ff_2_q, t_ff_3_q, t_ff_6_q, t_ff_7_q, t_ff_8_q, t_ff_10_q, t_ff_12_q,
       t_ff_14_q, t_ff_17_q, t_ff_19_q, t_ff_20_q, t_ff_21_q, t_ff_22_q, t_ff_23_q;

  Clock clock_1 (.out(clock_1_out));
  T_Flip_Flop t_ff_1 (.clk(clock_1_out), .T(clock_1_out), .Q(bit1), .reset(subclock), .en(1'b1));  // open: Qn, preset
  T_Flip_Flop t_ff_2 (.clk(clock_1_out), .T(bit1), .Q(t_ff_2_q), .reset(subclock), .en(1'b1));  // open: Qn, preset
  and and_1 (and_1_out, bit1, t_ff_2_q);
  and and_2 (and_2_out, and_1_out, t_ff_3_q);
  T_Flip_Flop t_ff_3 (.clk(clock_1_out), .T(and_1_out), .Q(t_ff_3_q), .reset(subclock), .en(1'b1));  // open: Qn, preset
  T_Flip_Flop t_ff_4 (.clk(clock_1_out), .T(and_2_out), .Q(bit4), .reset(subclock), .en(1'b1));  // open: Qn, preset
  and and_3 (and_3_out, and_2_out, bit4);
  T_Flip_Flop t_ff_5 (.clk(clock_1_out), .T(and_3_out), .Q(bit5), .reset(subclock), .en(1'b1));  // open: Qn, preset
  and and_4 (and_4_out, and_3_out, bit5);
  and and_5 (and_5_out, and_4_out, t_ff_6_q);
  T_Flip_Flop t_ff_6 (.clk(clock_1_out), .T(and_4_out), .Q(t_ff_6_q), .reset(subclock), .en(1'b1));  // open: Qn, preset
  T_Flip_Flop t_ff_7 (.clk(clock_1_out), .T(and_5_out), .Q(t_ff_7_q), .reset(subclock), .en(1'b1));  // open: Qn, preset
  and and_6 (and_6_out, and_5_out, t_ff_7_q);
  and and_7 (and_7_out, and_6_out, t_ff_8_q);
  T_Flip_Flop t_ff_8 (.clk(clock_1_out), .T(and_6_out), .Q(t_ff_8_q), .reset(subclock), .en(1'b1));  // open: Qn, preset
  and and_8 (subclock, bit1, bit4, bit5, bit9, bit12, bit14, bit15, bit17);
  and and_9 (and_9_out, and_7_out, bit9);
  T_Flip_Flop t_ff_9 (.clk(clock_1_out), .T(and_7_out), .Q(bit9), .reset(subclock), .en(1'b1));  // open: Qn, preset
  T_Flip_Flop t_ff_10 (
    .clk(clock_1_out), .T(and_9_out), .Q(t_ff_10_q), .reset(subclock), .en(1'b1));  // open: Qn, preset
  T_Flip_Flop t_ff_11 (.clk(subclock), .T(subclock), .Q(out_1), .en(1'b1));  // open: Qn, preset, reset
  and and_10 (and_10_out, and_9_out, t_ff_10_q);
  and and_11 (and_11_out, and_10_out, t_ff_12_q);
  T_Flip_Flop t_ff_12 (
    .clk(clock_1_out), .T(and_10_out), .Q(t_ff_12_q), .reset(subclock), .en(1'b1));  // open: Qn, preset
  T_Flip_Flop t_ff_13 (.clk(clock_1_out), .T(and_11_out), .Q(bit12), .reset(subclock), .en(1'b1));  // open: Qn, preset
  and and_12 (and_12_out, and_11_out, bit12);
  T_Flip_Flop t_ff_14 (
    .clk(clock_1_out), .T(and_12_out), .Q(t_ff_14_q), .reset(subclock), .en(1'b1));  // open: Qn, preset
  and and_13 (and_13_out, and_12_out, t_ff_14_q);
  and and_14 (and_14_out, and_13_out, bit14);
  T_Flip_Flop t_ff_15 (.clk(clock_1_out), .T(and_13_out), .Q(bit14), .reset(subclock), .en(1'b1));  // open: Qn, preset
  T_Flip_Flop t_ff_16 (.clk(clock_1_out), .T(and_14_out), .Q(bit15), .reset(subclock), .en(1'b1));  // open: Qn, preset
  and and_15 (and_15_out, and_14_out, bit15);
  and and_16 (and_16_out, and_15_out, t_ff_17_q);
  T_Flip_Flop t_ff_17 (
    .clk(clock_1_out), .T(and_15_out), .Q(t_ff_17_q), .reset(subclock), .en(1'b1));  // open: Qn, preset
  and and_17 (and_17_out, and_16_out, bit17);
  T_Flip_Flop t_ff_18 (.clk(clock_1_out), .T(and_16_out), .Q(bit17), .reset(subclock), .en(1'b1));  // open: Qn, preset
  T_Flip_Flop t_ff_19 (
    .clk(clock_1_out), .T(and_17_out), .Q(t_ff_19_q), .reset(subclock), .en(1'b1));  // open: Qn, preset
  and and_18 (and_18_out, and_17_out, t_ff_19_q);
  and and_19 (and_19_out, and_18_out, t_ff_20_q);
  T_Flip_Flop t_ff_20 (
    .clk(clock_1_out), .T(and_18_out), .Q(t_ff_20_q), .reset(subclock), .en(1'b1));  // open: Qn, preset
  T_Flip_Flop t_ff_21 (
    .clk(clock_1_out), .T(and_19_out), .Q(t_ff_21_q), .reset(subclock), .en(1'b1));  // open: Qn, preset
  and and_20 (and_20_out, and_19_out, t_ff_21_q);
  T_Flip_Flop t_ff_22 (
    .clk(clock_1_out), .T(and_20_out), .Q(t_ff_22_q), .reset(subclock), .en(1'b1));  // open: Qn, preset
  and and_21 (and_21_out, and_20_out, t_ff_22_q);
  and and_22 (and_22_out, and_21_out, t_ff_23_q);
  T_Flip_Flop t_ff_23 (
    .clk(clock_1_out), .T(and_21_out), .Q(t_ff_23_q), .reset(subclock), .en(1'b1));  // open: Qn, preset
  T_Flip_Flop t_ff_24 (.clk(clock_1_out), .T(and_22_out), .reset(subclock), .en(1'b1));  // open: Q, Qn, preset
endmodule
