// Logisim project Ativ02.circ as structural Verilog: 1 circuit, main circuit main
module main (
  input  X3,
  input  Y3,
  input  X2,
  input  Y2,
  input  X1,
  input  Y1,
  input  X0,
  input  Y0
);

  wire S0, S1, S2, S3;

  // _7_Segment_Display 7_segment_display_1: pin names not known; wires that end beside it: {X3, X2, X1, X0}, {Y3, Y2, Y1, Y0}
  // _7_Segment_Display 7_segment_display_2: pin names not known; wires that end beside it: {Y3, Y2, Y1, Y0}, {S3, S2, S1, S0}
  // BCD_to_7_Segment_decoder bcd_to_7_segment_decoder_1: pin names not known
  // BCD_to_7_Segment_decoder bcd_to_7_segment_decoder_2: pin names not known
  _7_Segment_Display u_7_segment_display_3 ();  // open: g, f, a, b, e, d, c, dp
  // BCD_to_7_Segment_decoder bcd_to_7_segment_decoder_3: pin names not known
  _74283 u_74283_1 (
    .pin1(S1), .pin2(Y1), .pin3(X1), .pin4(S0), .pin5(X0), .pin6(Y0), .pin15(Y2), .pin14(X2), .pin13(S2),
    .pin12(X3), .pin11(Y3), .pin10(S3));  // open: pin7, pin9

  // Other names for the same wires on the sheet: A[3:0] = {X3, X2, X1, X0}; B[3:0] = {Y3, Y2, Y1, Y0};
  //   Sf[3:0] = {S3, S2, S1, S0}
endmodule
