// Logisim project Ativ03.circ as structural Verilog: 1 circuit, main circuit main
module main (
  input  X0,
  input  X1,
  input  X2,
  input  X3,
  input  Y0,
  input  Y1,
  input  Y2,
  input  Y3
);

  wire adder_1_cout, adder_2_cout, X0Y0, X0Y1, X0Y2, X0Y3, X1Y0, X1Y1, X1Y2, X1Y3, X2Y0, X2Y1, X2Y2, X2Y3,
       X3Y0, X3Y1, X3Y2, X3Y3;
  wire [3:0] adder_3_out, adder_3_out_2;
  wire [7:0] bit_extender_1_out, bit_extender_2_out, bit_extender_3_out, bit_extender_4_out, shifter_1_out,
       shifter_2_out, shifter_3_out, Z1, Z2;

  assign bit_extender_1_out = {{4{1'b0}}, {X0Y3, X0Y2, X0Y1, X0Y0}};  // Bit_Extender bit_extender_1
  assign bit_extender_2_out = {{4{1'b0}}, {X2Y3, X2Y2, X2Y1, X2Y0}};  // Bit_Extender bit_extender_2
  and and_1 (X0Y0, X0, Y0);
  and and_2 (X0Y1, X0, Y1);
  and and_3 (X0Y2, X0, Y2);
  and and_4 (X0Y3, X0, Y3);
  and and_5 (X1Y0, X1, Y0);
  and and_6 (X1Y1, X1, Y1);
  and and_7 (X1Y2, X1, Y2);
  and and_8 (X1Y3, X1, Y3);
  assign bit_extender_3_out = {{4{1'b0}}, {X1Y3, X1Y2, X1Y1, X1Y0}};  // Bit_Extender bit_extender_3
  assign bit_extender_4_out = {{4{1'b0}}, {X3Y3, X3Y2, X3Y1, X3Y0}};  // Bit_Extender bit_extender_4
  Shifter shifter_1 (.in(bit_extender_3_out), .\dist (3'b001), .out(shifter_1_out));
  Shifter shifter_2 (.in(bit_extender_2_out), .\dist (3'b010), .out(shifter_2_out));
  and and_9 (X2Y0, X2, Y0);
  and and_10 (X2Y1, X2, Y1);
  and and_11 (X2Y2, X2, Y2);
  and and_12 (X2Y3, X2, Y3);
  Shifter shifter_3 (.in(bit_extender_4_out), .\dist (3'b010), .out(shifter_3_out));
  Hex_Digit_Display hex_digit_display_1 (.value(adder_3_out_2));  // open: dp
  Hex_Digit_Display hex_digit_display_2 (.value(adder_3_out));  // open: dp
  Adder adder_1 (.a(bit_extender_1_out), .b(shifter_1_out), .out(Z1), .cout(adder_1_cout));  // open: cin
  Adder adder_2 (.a(Z1), .b(shifter_2_out), .out(Z2), .cin(adder_1_cout), .cout(adder_2_cout));
  Adder adder_3 (.a(Z2), .b(shifter_3_out), .out({adder_3_out_2, adder_3_out}), .cin(adder_2_cout));  // open: cout
  and and_13 (X3Y0, X3, Y0);
  and and_14 (X3Y1, X3, Y1);
  and and_15 (X3Y2, X3, Y2);
  and and_16 (X3Y3, X3, Y3);

  // Notes on the sheet:
  //   1
  //   3
  //   2
  //   4
endmodule
