// Logisim project Exercicio4.circ as structural Verilog: 1 circuit, main circuit main
module main (
  input  in_1,
  input  PRESET,
  input  RESET,
  input  in_4,
  input  in_5
);

  wire and_1_out, and_2_out, and_3_out, and_5_out, clock_1_out, J0, J1, J2, K1, nor_1_out, not_1_out,
       not_3_out, not_4_out, X0, X1, X2, xor_1_out, xor_2_out, Y0, Y1, Y3;

  Clock clock_1 (.out(clock_1_out));
  xor xor_1 (xor_1_out, X0, X1);
  and and_1 (and_1_out, ~X2, in_1);  // AND_Gate
  or or_1 (Y0, xor_1_out, X2);
  J_K_Flip_Flop j_k_ff_1 (
    .J(J0), .clk(clock_1_out), .K(in_4), .Q(X0), .preset(PRESET), .en(1'b1), .reset(RESET));  // open: Qn
  or or_2 (J0, and_1_out, X1);
  not not_1 (not_1_out, X1);
  J_K_Flip_Flop j_k_ff_2 (
    .J(J1), .clk(clock_1_out), .K(K1), .Q(X1), .preset(PRESET), .en(1'b1), .reset(RESET));  // open: Qn
  or or_3 (Y1, X0, not_1_out);
  and and_2 (and_2_out, X0, in_1);
  and and_3 (and_3_out, ~in_1, X2);  // AND_Gate
  J_K_Flip_Flop j_k_ff_3 (
    .J(J2), .clk(clock_1_out), .K(in_5), .Q(X2), .preset(PRESET), .en(1'b1), .reset(RESET));  // open: Qn
  or or_4 (J1, and_2_out, and_3_out);
  not not_2 (K1, xor_2_out);
  xor xor_2 (xor_2_out, X0, in_1);
  not not_3 (not_3_out, X1);
  not not_4 (not_4_out, X2);
  and and_4 (Y3, not_3_out, not_4_out);
  Hex_Digit_Display hex_digit_display_1 (.value({Y3, X1, Y1, Y0}));  // open: dp
  and and_5 (and_5_out, X0, in_1, X1);
  nor nor_1 (nor_1_out, X0, in_1, X1);
  or or_5 (J2, and_5_out, nor_1_out);

  // Other names for the same wires on the sheet: Y2 = X1; DIR = in_1; K0 = in_4; K2 = in_5
endmodule
