// Logisim project Exercicio5.circ as structural Verilog: 1 circuit, main circuit main
module main (
  input  in_1,
  input  in_2
);

  wire and_1_out, and_2_out, and_3_out, and_4_out, and_5_out, and_6_out, and_7_out, and_8_out, and_9_out,
       and_10_out, and_11_out, and_12_out, and_13_out, and_14_out, and_15_out, clock_1_out, J0, J1, J2, K0,
       K1, K2, nor_1_out, X0, X1, X2;

  Clock clock_1 (.out(clock_1_out));
  J_K_Flip_Flop j_k_ff_1 (.J(J0), .clk(clock_1_out), .K(K0), .Q(X0), .en(1'b1));  // open: Qn, preset, reset
  nor nor_1 (nor_1_out, in_2, X1, X0);
  and and_1 (and_1_out, in_2, X1, ~X0);  // AND_Gate
  and and_2 (and_2_out, in_2, ~X1, ~X0);  // AND_Gate
  or or_1 (K2, and_2_out, and_3_out);
  and and_3 (and_3_out, ~in_2, X1, ~X0);  // AND_Gate
  or or_2 (J2, nor_1_out, and_1_out);
  J_K_Flip_Flop j_k_ff_2 (.J(J1), .clk(clock_1_out), .K(K1), .Q(X1), .en(1'b1));  // open: Qn, preset, reset
  and and_4 (and_4_out, ~in_2, X0, X2);  // AND_Gate
  and and_5 (and_5_out, in_2, X0, ~X2);  // AND_Gate
  and and_6 (and_6_out, ~in_2, ~X2, X0);  // AND_Gate
  and and_7 (and_7_out, in_2, X2, X0);
  J_K_Flip_Flop j_k_ff_3 (.J(J2), .clk(clock_1_out), .K(K2), .Q(X2), .en(1'b1));  // open: Qn, preset, reset
  or or_3 (J1, and_4_out, and_5_out);
  or or_4 (K1, and_6_out, and_7_out);
  Hex_Digit_Display hex_digit_display_1 (.value({in_1, X2, X1, X0}));  // open: dp
  and and_8 (and_8_out, ~in_2, ~X2, X1);  // AND_Gate
  and and_9 (and_9_out, ~in_2, X2, ~X1);  // AND_Gate
  and and_10 (and_10_out, in_2, ~X2, ~X1);  // AND_Gate
  and and_11 (and_11_out, in_2, X2, X1);
  and and_12 (and_12_out, ~in_2, ~X2, ~X1);  // AND_Gate
  and and_13 (and_13_out, ~in_2, X2, X1);  // AND_Gate
  and and_14 (and_14_out, in_2, X2, ~X1);  // AND_Gate
  and and_15 (and_15_out, in_2, ~X2, X1);  // AND_Gate
  or or_5 (J0, and_8_out, and_9_out, and_10_out, and_11_out);
  or or_6 (K0, and_12_out, and_13_out, and_14_out, and_15_out);

  // Other names for the same wires on the sheet: DIR = in_2
endmodule
