// Logisim project MaqEstados_PLB_35712.circ as structural Verilog: 1 circuit, main circuit main
module main (
  input  DIR,
  input  CLK,
  input  INICIO,
  output Q2,
  output Q1,
  output Q0
);

  wire and_1_out, and_2_out, and_3_out, and_4_out, and_5_out, and_6_out, J2, K0, K1, K2, not_1_out,
       not_2_out, not_3_out, not_4_out, not_5_out, not_6_out, not_7_out, not_8_out;

  not not_1 (not_1_out, DIR);
  not not_2 (not_2_out, Q1);
  not not_3 (not_3_out, DIR);
  not not_4 (not_4_out, Q0);
  not not_5 (not_5_out, Q2);
  not not_6 (not_6_out, Q1);
  not not_7 (not_7_out, DIR);
  not not_8 (not_8_out, Q2);
  and and_1 (and_1_out, DIR, Q1, Q0);
  and and_2 (and_2_out, not_1_out, not_2_out);
  and and_3 (and_3_out, DIR, Q1);
  and and_4 (and_4_out, not_3_out, not_4_out);
  and and_5 (and_5_out, DIR, not_5_out, not_6_out);
  and and_6 (and_6_out, not_7_out, not_8_out, Q1);
  or or_1 (J2, and_1_out, and_2_out);
  or or_2 (K2, and_2_out, and_3_out);
  or or_3 (K1, and_1_out, and_4_out, Q2);
  or or_4 (K0, and_5_out, and_6_out);
  J_K_Flip_Flop j_k_ff_1 (.J(J2), .clk(CLK), .K(K2), .Q(Q2), .preset(1'b0), .en(1'b1), .reset(INICIO));  // open: Qn
  J_K_Flip_Flop j_k_ff_2 (.J(1'b1), .clk(CLK), .K(K1), .Q(Q1), .preset(INICIO), .en(1'b1), .reset(1'b0));  // open: Qn
  J_K_Flip_Flop j_k_ff_3 (.J(1'b1), .clk(CLK), .K(K0), .Q(Q0), .preset(INICIO), .en(1'b1), .reset(1'b0));  // open: Qn
  Hex_Digit_Display hex_digit_display_1 (.value({1'b0, Q2, Q1, Q0}));  // open: dp
endmodule
