// Logisim project Q1.circ as structural Verilog: 1 circuit, main circuit main
module main (
);

  wire and_1_out, and_2_out, clock_1_out, j_k_ff_1_q, j_k_ff_2_q, or_1_out, preset_out, reset_out, t_ff_1_q;
  wire [2:1] t_ff_2_q;

  Clock clock_1 (.out(clock_1_out));
  Button reset (.out(reset_out));
  Button preset (.out(preset_out));
  T_Flip_Flop t_ff_1 (.clk(clock_1_out), .T(clock_1_out), .Q(t_ff_1_q), .reset(reset_out));  // open: Qn, preset, en
  J_K_Flip_Flop j_k_ff_1 (
    .J(1'b1), .clk(clock_1_out), .K(1'b1), .Q(j_k_ff_1_q), .reset(reset_out));  // open: Qn, preset, en
  T_Flip_Flop t_ff_2 (
    .clk(t_ff_1_q), .T(t_ff_1_q), .Q(t_ff_2_q[1]), .preset(preset_out), .en(1'b1));  // open: Qn, reset
  J_K_Flip_Flop j_k_ff_2 (
    .J(j_k_ff_1_q), .clk(clock_1_out), .K(j_k_ff_1_q), .Q(j_k_ff_2_q), .reset(reset_out));  // open: Qn, preset, en
  T_Flip_Flop t_ff_3 (
    .clk(or_1_out), .T(or_1_out), .Q(t_ff_2_q[2]), .preset(preset_out), .en(1'b1));  // open: Qn, reset
  and and_1 (and_1_out, j_k_ff_1_q, j_k_ff_2_q);
  and and_2 (and_2_out, ~j_k_ff_1_q, ~j_k_ff_2_q);  // AND_Gate
  or or_1 (or_1_out, and_1_out, and_2_out);
  Hex_Digit_Display hex_digit_display_1 (.value({1'b1, t_ff_2_q, 1'b0}));  // open: dp
endmodule
